# Fritzing sketch IoT_Aquarium (saved by Fritzing 0.9.3b)
breadboards: 2

parts:
  HC-SR04_Ultrasonic_sensor = hc-sr04
  Nokia_5110_LCD_Module1 = Nokia 5110 LCD
  SM1 = 28BYJ-48 Stepper Motor [part_number=28BYJ-48]
  Driver1 = 28BYJ-48 Driver Module [part_number=ULN2003 package=THT]
  U1 = 4-Channel 5v Relay Shield [package=relay-4ch5v10a]
  Raspberry_Pi_1 = Raspberry Pi 4 [part_number=RPI-4-b]
  IC1 = Rasberry Pi NIOR Camera [chip_label=IC package="DIP (Dual Inline) [THT]"]  # not connected
  S1 = Pushbutton [package="[SMD]"]
  S2 = Pushbutton [package="[SMD]"]
  S3 = Pushbutton [package="[SMD]"]
  S4 = Pushbutton [package="[SMD]"]
  LED1 = LED - 5mm [color="Red (633nm)" package="5 mm [THT]"]
  LED2 = LED - 5mm [color="Red (633nm)" package="5 mm [THT]"]
  LED3 = LED - 5mm [color="Red (633nm)" package="5 mm [THT]"]
  S5 = Pushbutton [package="[THT]"]
  R1 = Resistor [tolerance=±5% resistance=220 package=THT]
  R2 = Resistor [tolerance=±5% resistance=220 package=THT]
  R3 = Resistor [tolerance=±5% resistance=220 package=THT]
  R4 = Resistor [tolerance=±5% resistance=1k package=THT]
  R5 = Resistor [tolerance=±5% resistance=1k package=THT]
  R6 = Resistor [tolerance=±5% resistance=1k package=THT]
  R7 = Resistor [tolerance=±5% resistance=1k package=THT]
  C1 = Tantalum Capacitor [capacitance=1μF package="100 mil [THT, tantalum]"]
  R9 = Photocell (LDR) [package=THT]
  IC2 = L293D [package=THT]  # not connected
  R10 = Resistor [tolerance=±5% resistance=1k package=THT]
  VCC1 = 4 x AAA Battery Mount
  R11 = Resistor [tolerance=±5% resistance=2.2k package=THT]
  Stepper_motor = DC Motor
  R12 = Resistor [tolerance=±5% resistance=470 package=THT]
  R13 = Resistor [tolerance=±5% resistance=330 package=THT]

nets:
  N1: HC-SR04_Ultrasonic_sensor.VCC, VCC1.+
  N2: HC-SR04_Ultrasonic_sensor.Trig, Raspberry_Pi_1.GPIO21
  N3: HC-SR04_Ultrasonic_sensor.Echo, R13.Pin_0
  N4: HC-SR04_Ultrasonic_sensor.GND, VCC1.-, R12.Pin_1
  N5: Nokia_5110_LCD_Module1.SCE, Raspberry_Pi_1.GPIO13
  N6: Nokia_5110_LCD_Module1.RST, Raspberry_Pi_1.GPIO6
  N7: Nokia_5110_LCD_Module1.D/C, Raspberry_Pi_1.GPIO11
  N8: Nokia_5110_LCD_Module1.DN(MOSI), Nokia_5110_LCD_Module1.SCLK, Nokia_5110_LCD_Module1.DN(MODI)_(out), Nokia_5110_LCD_Module1.SCLK_(out), Driver1.Vmotor, Raspberry_Pi_1.5V
  GND: Nokia_5110_LCD_Module1.LED, Nokia_5110_LCD_Module1.LED_(out), Driver1.GND, Raspberry_Pi_1.GND, S1.Pin_3, S1.Pin_4, S2.Pin_3, S2.Pin_4, S3.Pin_3, S3.Pin_4, S4.Pin_3, S4.Pin_4, LED1.cathode, LED2.cathode, LED3.cathode, S5.Pin_3, S5.Pin_4, C1.-
  N9: SM1.blue-pin, Driver1.blue-pin
  N10: SM1.pink-pin, Driver1.pink-pin
  N11: SM1.yellow-pin, Driver1.yellow-pin
  N12: SM1.orange-pin, Driver1.orange-pin
  N13: SM1.red-pin, Driver1.red-pin
  N14: Driver1.IN1, Raspberry_Pi_1.GPIO7
  N15: Driver1.IN2, Raspberry_Pi_1.GPIO8
  N16: Driver1.IN3, Raspberry_Pi_1.GPIO25
  N17: Driver1.IN4, Raspberry_Pi_1.GPIO24
  N18: U1.K4-Off, Stepper_motor.pin_2
  N19: Raspberry_Pi_1.3v3, R4.Pin_0, R5.Pin_0, R6.Pin_0, R7.Pin_0, R10.Pin_0, R11.Pin_0
  N20: Raspberry_Pi_1.GPIO17, S1.Pin_1, S1.Pin_2, R4.Pin_1
  N21: Raspberry_Pi_1.GPIO27, S2.Pin_1, S2.Pin_2, R6.Pin_1
  N22: Raspberry_Pi_1.GPIO22, S3.Pin_1, S3.Pin_2, R5.Pin_1
  N23: Raspberry_Pi_1.GPIO10, S4.Pin_1, S4.Pin_2, R10.Pin_1
  N24: Raspberry_Pi_1.GPIO9, S5.Pin_1, S5.Pin_2, R7.Pin_1
  N25: Raspberry_Pi_1.GPIO20, R12.Pin_0, R13.Pin_1
  N26: Raspberry_Pi_1.GPIO12, C1.+, R9.pin_0
  N27: Raspberry_Pi_1.GPIO23, R3.Pin_1
  N28: Raspberry_Pi_1.GPIO18, R1.Pin_1
  N29: Raspberry_Pi_1.GPIO15, R2.Pin_1
  N30: LED1.anode, R3.Pin_0
  N31: LED2.anode, R2.Pin_0
  N32: LED3.anode, R1.Pin_0
  N33: R9.pin_1, R11.Pin_1

notes:
  DC Pump
  DC Pump --> 3-6V
  HC-SR04 --> 5V
  Nokia LCD --> 3.3V
  Relay --> 3.75-6V
  Stepper Motor --> 5V
  Buttons --> 3.3V
  5V
  3.3V
  6V

custom parts:
  Nokia 5110 LCD: Nokia 5110 Graphic 84*48 LCD module such as the Sparkfun LCD-10168 or the clones from Ebay. There is example code for the Arduino available from the Sparkfun site in https://learn.sparkfun.com/tutorials/graphic-lcd-hookup-guide This is a 3.3V device, if you are running it from a 5V micro you need a 5V tolorant level translator such as the 74ahc367 to protect the signal imputs. Rafa G. did a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
  28BYJ-48 Stepper Motor: Unipolar Stepper Motor 28BYJ-48 Top coil - pink & orange Bottom coil - blue & yellow Common rail - red Connector pins: blue - pink - yellow - orange - red
  28BYJ-48 Driver Module: ULN2003 Driver Module for the 28BYJ-48 Unipolar Stepper Motor LED A - Blue wire - Bottom coil left LED B - Pink wire - Top coil left LED C - Yellow wire - Bottom coil right LED D - Orange wire - Top coil right Common rail - red Connector pins: blue - pink - yellow - orange - red Control pins - IN1 to IN4 Power pins - GND & Vmotor (5-12V) On/Off jumper (if removed, power to motor is cut).
  4-Channel 5v Relay Shield: 4 Channel 5v Relay Shield w. 2x SPD-06VDC-SD-C
  Raspberry Pi 4: The RPi4, a faster version of the awesome Raspberry Pi 2 B ARM Board with 40 pin gpio. Ready for special Raspberry Pi B+ and RPi2 Hat (Hardware attached (on) top)
  Rasberry Pi NIOR Camera: Camera
